// Digital circuit inst-decoder-verilog.dig as structural Verilog
module inst_decoder_verilog (
  input  [31:0] instruction_code,
  input  PC_EN,
  output [4:0] rd,
  output [4:0] rs1,
  output [4:0] rs2,
  output [6:0] imm_2531,
  output [19:0] imm_1231,
  output [11:0] imm_2031,
  output [31:0] invalid_op,
  output [7:0] mechine_op,
  output [5:0] csr_op,
  output [8:0] jmp_op,
  output [18:0] alu_op,
  output [8:0] mem_op,
  output cust_op
);

  inst_decoder_verilog #(.applicationType("IVERILOG"), .iverilogOptions("-y C:\\\\Users\\\\gwx1330001\\\\Documents\\\\riscv-mcu\\\\verilog")) u_inst_decoder_verilog (
    .instruction_code(instruction_code), .en(PC_EN), .invalid_instruction(invalid_op), .alu_op(alu_op),
    .jmp_op(jmp_op), .mem_op(mem_op), .cust_op(cust_op), .csr_op(csr_op), .mechie_op(mechine_op), .rd(rd),
    .rs1(rs1), .rs2(rs2), .imm_2531(imm_2531), .imm_1231(imm_1231), .imm_2032(imm_2031));

  // Other names for the same wires on the sheet: mechie_op[7:0] = mechine_op
endmodule

/* Code of inst_decoder_verilog:
module inst_decoder_verilog(
    input [31:0] instruction_code,
    input en,
    output wire [31:0] invalid_instruction,
    output wire [18:0] alu_op,
    output wire [8:0] jmp_op,
    output wire [8:0] mem_op,
    output wire cust_op,
    output wire [5:0] csr_op,
    output wire [7:0] mechie_op,
    output wire [4:0] rd, rs1, rs2,
    output wire [6:0] imm_2531,
    output wire [19:0] imm_1231,
    output wire [11:0] imm_2032
);

instruction_decoder dut(
        .instruction_code(instruction_code),
        .en(en),
        .invalid_instruction(invalid_instruction),
        .alu_op(alu_op),
        .jmp_op(jmp_op),
        .mem_op(mem_op),
        .cust_op(cust_op),
        .csr_op(csr_op),
        .mechie_op(mechie_op),
        .rd(rd),
        .rs1(rs1),
        .rs2(rs2),
        .imm_2531(imm_2531),
        .imm_1231(imm_1231),
        .imm_2032(imm_2032)
    );

endmodule
*/
