// Digital circuit risc-v-mcu.dig as structural Verilog
module risc_v_mcu (
  input  Clock,
  input  TimerClock,
  input  UartClock,
  input  IICClock,
  input  GPIO_in1,
  input  GPIO_in2,
  input  GPIO_in3,
  input  GPIO_in4,
  input  GPIO_in5,
  input  GPIO_in6,
  input  GPIO_in7,
  input  GPIO_in8,
  input  GPIO_in9,
  input  GPIO_in10,
  input  RX,
  input  SDA_in,
  input  [7:0] ssd_bytein,
  output GPIO_1,
  output GPIO_2,
  output GPIO_3,
  output GPIO_4,
  output GPIO_5,
  output GPIO_6,
  output GPIO_7,
  output GPIO_8,
  output GPIO_9,
  output GPIO_10,
  output TX,
  output SDA_out,
  output SCL,
  output [23:0] Addr_ssd,
  output ssd_en
);

  wire Addr_csr1, addrflag_boot, addrflag_mem, addrflag_memtmp, addrflag_peripheral, addrflag_ssd, and_4_out,
       ard_en, crd_en, Cust_op, data_1, Data_csr, data_dma, data_mem, debug_data, debug_info, dma_addr,
       int_gatesrc, int_gpiocode, int_iiccode, int_peripheral, int_peripheralcode, int_timer, int_uartcode,
       jrd_en, lrd_en, memgpio_en, memiic_en, memplic_en, memuart_en, mip_cur, mip_set, mip_seten, mret,
       nor_1_out, not_1_out, Oe_dma, Oe_mem, Oe_memop, or_3_out, Out_csr1, Out_csr2, PC_except, PC_inited,
       PC_jmp, PC_jmpen, rd_en, rs1_data, rs2_data, storebytes_size, We_dma, We_mem;
  wire [4:0] driver_17_out, rd, rs1, rs2;
  wire [5:0] csr_op;
  wire [6:0] imm_7;
  wire [7:0] mechine_op;
  wire [8:0] jmp_op, mem_op;
  wire [11:0] imm_12;
  wire [18:0] alu_op;
  wire [19:0] imm_20;
  wire [23:0] addr_real;
  wire [29:24] mem_addr;
  wire [30:24] PC_exec;
  wire [31:0] Addr_except, Addr_jmp, Addr_jmpto, ard_out, crd_out, data_memgpio, data_memiic, data_memplic,
       data_memrd, data_memrdin, data_memuart, instruction_code, Invalid_op, IR_q, jrd_out, lrd_out, PC_next,
       PC_p6, rd_out;

  nor nor_1 (nor_1_out, addrflag_peripheral, addrflag_ssd);
  and and_1 (ssd_en, addrflag_ssd, ~Oe_dma, Oe_memop);  // And
  and and_2 (Oe_mem, nor_1_out, Oe_memop);
  and and_3 (Oe_dma, addrflag_ssd, addrflag_peripheral, Oe_memop);
  or or_1 (PC_jmpen, PC_jmp, PC_except);
  and and_4 (and_4_out, PC_jmp, ~PC_except);  // And
  or or_2 (rd_en, jrd_en, ard_en, crd_en, lrd_en);
  assign data_memrdin = memplic_en ? data_memplic : 32'bz;  // Driver driver_1
  assign data_memrdin = memgpio_en ? data_memgpio : 32'bz;  // Driver driver_2
  assign Addr_jmpto = and_4_out ? Addr_jmp : 32'bz;  // Driver driver_3
  assign data_memrdin = memuart_en ? data_memuart : 32'bz;  // Driver driver_4
  not not_1 (not_1_out, PC_inited);
  assign data_memrdin = ssd_en ? {{24{1'b0}}, ssd_bytein} : 32'bz;  // Driver driver_5
  assign data_memrdin = or_3_out ? data_memrd : 32'bz;  // Driver driver_6
  assign {addrflag_boot, PC_exec[30:26], addrflag_memtmp, PC_exec[24], addr_real} = not_1_out ? 32'h80000000 : 32'bz;  // Driver driver_7
  assign Addr_jmpto = PC_except ? Addr_except : 32'bz;  // Driver driver_8
  assign rd_out = jrd_en ? jrd_out : 32'bz;  // Driver driver_9
  assign rd_out = ard_en ? ard_out : 32'bz;  // Driver driver_10
  assign rd_out = crd_en ? crd_out : 32'bz;  // Driver driver_11
  assign rd_out = lrd_en ? lrd_out : 32'bz;  // Driver driver_12
  assign data_memrdin = memiic_en ? data_memiic : 32'bz;  // Driver driver_13
  or or_3 (or_3_out, Oe_dma, Oe_mem);
  assign PC_next = not_1_out ? 32'h80000004 : 32'bz;  // Driver driver_14
  // program_counter PC: pin names not known; wires that end beside it: 1'b1, Clock, {addrflag_boot, PC_exec[30:26], addrflag_memtmp, PC_exec[24], addr_real}, Addr_jmpto, PC_jmpen, PC_p6
  assign PC_next = PC_inited ? PC_p6 : 32'bz;  // Driver driver_15
  // mechine_op_unit mechine_op_unit_1: pin names not known; wires that end beside it: mechine_op, mret
  // cust_ctrl cust_ctrl_1: pin names not known; wires that end beside it: instruction_code, Cust_op, Clock, PC_inited
  // csr csr_1: pin names not known; wires that end beside it: csr_op, rs1_data, imm_12, rs1, Clock, Out_csr1, crd_en, Addr_csr1, crd_out, Data_csr
  Register #(.Bits(32)) IR (.D(PC_next), .C(Clock), .en(1'b1), .Q(IR_q));
  assign {addrflag_boot, PC_exec[30:26], addrflag_memtmp, PC_exec[24], addr_real} = PC_inited ? IR_q : 32'bz;  // Driver driver_16
  // instuction_jump_unit instuction_jump_unit_1: pin names not known; wires that end beside it: jmp_op, {addrflag_boot, PC_exec[30:26], addrflag_memtmp, PC_exec[24], addr_real}, PC_next, rs1_data, rs2_data, imm_12, imm_20, imm_7, rd, Addr_jmp, jrd_out, jrd_en, PC_jmp
  // memory_operation_unit memory_operation_unit_1: pin names not known; wires that end beside it: mem_op, data_memrdin, rs1_data, rs2_data, imm_12, imm_7, rd, imm_20, We_mem, {addrflag_peripheral, addrflag_ssd, mem_addr, Addr_ssd}, data_mem, storebytes_size, Oe_memop, lrd_en, lrd_out
  // alu alu_1: pin names not known; wires that end beside it: alu_op, rs1_data, rs2_data, imm_12, Clock, ard_out, ard_en, Invalid_op
  inst_decoder_verilog inst_decoder_verilog_1 (
    .instruction_code(instruction_code), .PC_EN(1'b1), .rd(rd), .rs1(rs1), .rs2(rs2), .imm_2531(imm_7),
    .imm_1231(imm_20), .imm_2031(imm_12), .invalid_op(Invalid_op), .mechine_op(mechine_op), .csr_op(csr_op),
    .jmp_op(jmp_op), .alu_op(alu_op), .mem_op(mem_op), .cust_op(Cust_op));
  and and_5 (addrflag_mem, addrflag_memtmp, ~addrflag_boot);  // And
  // PLIC plic_1: pin names not known; wires that end beside it: Clock, TimerClock, {addrflag_peripheral, addrflag_ssd, mem_addr, Addr_ssd}, data_mem, We_mem, {addrflag_peripheral, addrflag_ssd, mem_addr, Addr_ssd}, mip_cur, int_peripheralcode, mret, data_memplic, memplic_en, mip_set, mip_seten, int_timer, int_gatesrc
  assign driver_17_out = rd_en ? rd : 5'bz;  // Driver driver_17
  PullDown #(.Bits(5)) pulldown_1 (.out(driver_17_out));
  // risc_v_registers Common_Regs: pin names not known; wires that end beside it: rs1, rd_out, Clock, driver_17_out, rs2, 5'b01110, rs1_data, rs2_data, debug_data
  // boot_rom Boot_Rom: pin names not known; wires that end beside it: addr_real, addrflag_boot, instruction_code
  // memory memory_1: pin names not known; wires that end beside it: dma_addr, data_dma, We_dma, 1'b0, 4'b0001, Clock, {addrflag_peripheral, addrflag_ssd, mem_addr, Addr_ssd}, Oe_dma, data_1, data_memrd
  // int_except_unit int_except_unit_1: pin names not known; wires that end beside it: Data_csr, crd_en, Addr_csr1, Clock, Addr_csr1, {12{1'b0}}, Invalid_op, {addrflag_boot, PC_exec[30:26], addrflag_memtmp, PC_exec[24], addr_real}, instruction_code, PC_next, mret, mip_set, mip_seten, Out_csr1, Out_csr2, PC_except, Addr_except, mip_cur, debug_info
  // i2c_controller i2c_controller_1: pin names not known; wires that end beside it: IICClock, SDA_in, {addrflag_peripheral, addrflag_ssd, mem_addr, Addr_ssd}, data_mem, We_mem, {addrflag_peripheral, addrflag_ssd, mem_addr, Addr_ssd}, int_peripheral, Clock, SDA_out, SCL, data_memiic, memiic_en, int_iiccode
  PullDown #(.Bits(32)) pulldown_2 (.out(data_memrd));
  // memory Momery: pin names not known; wires that end beside it: {addrflag_peripheral, addrflag_ssd, mem_addr, Addr_ssd}, data_mem, We_mem, Oe_mem, storebytes_size, Clock, {addrflag_boot, PC_exec[30:26], addrflag_memtmp, PC_exec[24], addr_real}, addrflag_mem, data_memrd, instruction_code
  // int_bus int_bus_1: pin names not known; wires that end beside it: Clock, int_gatesrc, int_uartcode, int_gpiocode, int_iiccode, int_peripheral, int_peripheralcode
  // gpio gpio_1: pin names not known; wires that end beside it: Clock, {addrflag_peripheral, addrflag_ssd, mem_addr, Addr_ssd}, data_mem, We_mem, {addrflag_peripheral, addrflag_ssd, mem_addr, Addr_ssd}, int_peripheral, GPIO_in1, GPIO_in2, GPIO_in3, GPIO_in4, GPIO_in5, GPIO_in6, GPIO_in7, GPIO_in8, GPIO_in9, GPIO_in10, data_memgpio, memgpio_en, int_gpiocode, GPIO_1, GPIO_2, GPIO_3, GPIO_4, GPIO_5, GPIO_6, GPIO_7, GPIO_8, GPIO_9, GPIO_10
  // uart uart_1: pin names not known; wires that end beside it: {addrflag_peripheral, addrflag_ssd, mem_addr, Addr_ssd}, data_mem, We_mem, {addrflag_peripheral, addrflag_ssd, mem_addr, Addr_ssd}, int_peripheral, RX, Clock, UartClock, TX, data_memuart, memuart_en, int_uartcode, data_dma, dma_addr, We_dma

  // Other names for the same wires on the sheet: Addr_csrw = Addr_csr1; c = Clock; gpio_out1 = GPIO_1;
  //   gpio_out2 = GPIO_2; gpio_out3 = GPIO_3; gpio_out4 = GPIO_4; gpio_out5 = GPIO_5; gpio_out6 = GPIO_6;
  //   gpio_out7 = GPIO_7; gpio_out8 = GPIO_8; gpio_out9 = GPIO_9; gpio_out10 = GPIO_10; iic_clock = IICClock;
  //   addr_iop[23:0] = Addr_ssd; mem_addr (some bits) = {addrflag_peripheral, addrflag_ssd, Addr_ssd};
  //   Oe_ssd = ssd_en; PC_exec (some bits) = {addrflag_boot, addrflag_memtmp, addr_real};
  //   data_memssd[7:0] = ssd_bytein; Timer_clock = TimerClock; uart_clock = UartClock

  // Notes on the sheet:
  //   Clock: Hz: 50000
  //   TimerClock: Hz: 100
  //   UartClock: Hz: 50000
  //   IICClock: Hz: 50000
  //   Reg Bus
  //   Memory Bus
  //   Instruction Execution Unit
  //   Instruction Program Counter Bus
  //   Instruction Decoder
  //   Exception  Interrupt Unit
  //   DMA Controller
  //   Peripheral IIC
  //   Storage
  //   Peripheral GPIO
  //   Peripheral UART
endmodule
